# Fritzing sketch Step5 (saved by Fritzing 0.9.3b)
breadboards: 1

parts:
  Raspberry_Pi1 = Raspberry Pi 2
  LED7 = LED - 5mm [color="Red (633nm)" package="5 mm [THT]"]
  LED6 = LED - 5mm [color="Yellow (595nm)" package="5 mm [THT]"]
  LED5 = LED - 5mm [color="Green (555nm)" package="5 mm [THT]"]
  LED4 = LED - 5mm [color="Blue (430nm)" package="5 mm [THT]"]
  LED3 = LED - 5mm [color="Green (555nm)" package="5 mm [THT]"]
  LED2 = LED - 5mm [color="Yellow (595nm)" package="5 mm [THT]"]
  R7 = Resistor [tolerance=±5% resistance=330 package=THT]
  R6 = Resistor [tolerance=±5% resistance=330 package=THT]
  R5 = Resistor [tolerance=±5% resistance=330 package=THT]
  R4 = Resistor [tolerance=±5% resistance=330 package=THT]
  R3 = Resistor [tolerance=±5% resistance=330 package=THT]
  R2 = Resistor [tolerance=±5% resistance=330 package=THT]
  R1 = Resistor [tolerance=±5% resistance=330 package=THT]
  LED1 = LED - 5mm [color="Red (633nm)" package="5 mm [THT]"]
  S1 = Pushbutton [package="[THT]"]
  S2 = Pushbutton [package="[THT]"]

nets:
  N1: Raspberry_Pi1.GPIO4, S1.Pin_1, S1.Pin_2
  N2: Raspberry_Pi1.GPIO17, R1.Pin_1
  N3: Raspberry_Pi1.GPIO27, R3.Pin_1
  N4: Raspberry_Pi1.GPIO22, R4.Pin_1
  N5: Raspberry_Pi1.GPIO5, S2.Pin_3, S2.Pin_4
  N6: Raspberry_Pi1.GND, LED7.anode, LED6.anode, LED5.anode, LED4.anode, LED3.anode, LED2.anode, LED1.anode
  N7: Raspberry_Pi1.GPIO25, R7.Pin_1
  N8: Raspberry_Pi1.GPIO24, R6.Pin_1
  N9: Raspberry_Pi1.GPIO23, R5.Pin_1
  N10: Raspberry_Pi1.GPIO18, R2.Pin_1
  N11: Raspberry_Pi1.5V, S1.Pin_3, S1.Pin_4, S2.Pin_1, S2.Pin_2
  N12: LED7.cathode, R7.Pin_0
  N13: LED6.cathode, R6.Pin_0
  N14: LED5.cathode, R5.Pin_0
  N15: LED4.cathode, R4.Pin_0
  N16: LED3.cathode, R3.Pin_0
  N17: LED2.cathode, R2.Pin_0
  N18: R1.Pin_0, LED1.cathode
